# Fritzing sketch MeterClock-fritzing-schematic (saved by Fritzing 0.9.9b)
breadboards: 1

parts:
  RE1 = Rotary Encoder [package=THT]
  Part1 = Arduino Nano (Rev3.0)
  Part2 = LED Matrix - Serial Interface - Red/Green/Blue
  ZS-042_RTC1 = ZS-042 RTC Module
  R4 = Resistor [tolerance=±5% resistance=10k power=0.25 package=THT]
  R6 = Resistor [tolerance=±5% resistance=10k power=0.25 package=THT]
  C1 = Ceramic Capacitor [capacitance=10nF voltage=35V package="200 mil [THT, multilayer]"]
  C2 = Ceramic Capacitor [capacitance=10nF voltage=35V package="200 mil [THT, multilayer]"]
  R1 = Resistor [tolerance=±1% resistance=2.7k package="1206 [SMD]"]
  R2 = Resistor [tolerance=±1% resistance=2.7k package="1206 [SMD]"]
  S1 = Square Pushbutton
  S2 = Square Pushbutton
  C3 = Ceramic Capacitor [capacitance=1µF package="200 mil [THT, multilayer]"]
  C4 = Ceramic Capacitor [capacitance=1µF package="200 mil [THT, multilayer]"]
  R7 = Resistor [tolerance=±5% resistance=80k power=0.25 package=THT]
  R8 = Resistor [tolerance=±5% resistance=80k power=0.25 package=THT]
  R9 = Resistor [tolerance=±5% resistance=18k power=0.25 package=THT]
  R10 = Resistor [tolerance=±5% resistance=18k power=0.25 package=THT]
  R11 = Resistor [tolerance=±5% resistance=10k power=0.25 package=THT]
  R12 = Resistor [tolerance=±5% resistance=10k power=0.25 package=THT]

nets:
  N1: RE1.EncoderPinA, R4.Pin_0, R6.Pin_0
  GND: RE1.EncoderPinC, Part1.GND, Part2.GND, ZS-042_RTC1.GND, C1.0, C2.0, R1.Pin_1, R2.Pin_1, S1.leg0, S2.leg0, C3.0, C4.0
  N2: RE1.EncoderPinB, R11.Pin_1, R12.Pin_0
  N3: Part1.D2, R4.Pin_1, C1.1
  N4: Part1.D3, C2.1, R11.Pin_0
  N5: Part1.D5, R1.Pin_0
  N6: Part1.D6, R2.Pin_0
  N7: Part1.D8, Part2.SCK
  N8: Part1.D9, Part2.CS
  N9: Part1.D10, Part2.MISO
  5V: Part1.5V, Part2.VCC, ZS-042_RTC1.VCC, R6.Pin_1, R7.Pin_1, R8.Pin_1, R12.Pin_1
  N10: Part1.A7, C4.1, R10.Pin_1
  N11: Part1.A6, C3.1, R9.Pin_1
  N12: Part1.A5, ZS-042_RTC1.SCL
  N13: Part1.A4, ZS-042_RTC1.SDA
  N14: S1.leg1, R8.Pin_0, R10.Pin_0
  N15: S2.leg1, R7.Pin_0, R9.Pin_0

notes:
  D5 and D6 drive Analog Meters at 1mA max correspnds to 60% 3V.
  Resistors connect to analog millAmp Meters
